# Fritzing sketch cessna-knobox (saved by Fritzing 0.9.4)

parts:
  M1 = STM32F103C8T6 blue mini board
  R3 = Resistor [tolerance=±5% resistance=15k package="2010 [SMD]"]
  R2 = Resistor [tolerance=±5% resistance=15k package="2010 [SMD]"]
  R1 = Resistor [tolerance=±5% resistance=15k package="2010 [SMD]"]
  R4 = Resistor [tolerance=±5% resistance=15k package="2010 [SMD]"]
  R5 = Resistor [tolerance=±5% resistance=15k package="2010 [SMD]"]
  S1 = Taiway 100-SP-X-T1 SPDT Miniature Toggle Switch [part_number=100-SP-X-T1-0-0-B1-M2 package=THT]
  S2 = Taiway 100-SP-X-T1 SPDT Miniature Toggle Switch [part_number=100-SP-X-T1-0-0-B1-M2 package=THT]
  S3 = Taiway 100-SP-X-T1 SPDT Miniature Toggle Switch [part_number=100-SP-X-T1-0-0-B1-M1 package=THT]
  S4 = Taiway 100-SP-X-T1 SPDT Miniature Toggle Switch [part_number=100-SP-X-T1-0-0-B1-M1 package=THT]
  R6 = Slide Potentiometer [maximum_resistance=100kΩ]
  R7 = Slide Potentiometer [maximum_resistance=100kΩ]
  J1 = female pin header, 1 pin [form="♀ (female)"]
  J2 = female pin header, 1 pin [form="♀ (female)"]

nets:
  N1: M1.B14, R4.Pin_1, S4.L2
  N2: M1.B15, R5.Pin_1, S4.L1
  N3: M1.A8, R1.Pin_1, S1.L2
  N4: M1.A9, R2.Pin_1, S2.L2
  N5: M1.A10, R3.Pin_1, S3.L2
  N6: M1.5V, R3.Pin_0, R2.Pin_0, R1.Pin_0, R4.Pin_0, R5.Pin_0
  N7: M1.G, M1.GND, S1.COM, S2.COM, S3.COM, S4.COM, R6.leg2, R7.leg2, J2.pin1
  N8: M1.3.3V, R6.leg1, R7.leg1, J1.pin1
  N9: M1.A1, R6.wiper
  N10: M1.A2, R7.wiper
